# Fritzing sketch CITI721 (saved by Fritzing 0.9.2b)
breadboards: 2

parts:
  LCD = LCD screen
  PIR = PIR sensor
  LED_D = RGB LED - (4 legs) [package="5 mm [THT]"]
  LED_I = RGB LED - (4 legs) [package="5 mm [THT]"]
  STD_Servo_(I) = Basic Servo
  STD_Servo_(D) = Basic Servo
  R1 = TRIMPOT [package=3386u]
  R2 = Resistor [tolerance=±5% resistance=220 package="2010 [SMD]"]
  RTC = Real Time Clock Module - DS1307 RTC Breakout Board
  R3 = Resistor [tolerance=±5% resistance=220 package="2010 [SMD]"]
  R4 = Resistor [tolerance=±5% resistance=220 package="2010 [SMD]"]
  R5 = Resistor [tolerance=±5% resistance=220 package="2010 [SMD]"]
  R7 = Resistor [tolerance=±5% resistance=220 package="2010 [SMD]"]
  R8 = Resistor [tolerance=±5% resistance=220 package="2010 [SMD]"]
  SPKR1 = Loudspeaker  # not connected
  CR_Servo_(I) = Basic Servo
  CR_Servo_(D) = Basic Servo
  R10 = Resistor [tolerance=±5% resistance=1M package="2512 [SMD]"]
  Sensor_cap_2 = TOUCH [package=touch2]
  Sensor_cap_1 = TOUCH [package=touch2]
  R11 = Resistor [tolerance=±5% resistance=1M package="2512 [SMD]"]
  Sensor_cap_3 = TOUCH [package=touch2]
  R12 = Resistor [tolerance=±5% resistance=1M package="2512 [SMD]"]
  R6 = Resistor [tolerance=±5% resistance=220 package="2010 [SMD]"]
  Parte1 = Arduino Mega 2560 (Rev3)
  SPKR2 = Loudspeaker  # not connected
  MIC1 = Microphone  # not connected
  U1 = 3.5mm Audio Jack [package=audio-jack-3.5mm-smd]  # not connected
  U3 = STA540 [package=multiwatt15]  # not connected

nets:
  VCC: LCD.VDD, PIR.VDD, STD_Servo_(I).vcc, STD_Servo_(D).vcc, R1.CW, R2.Pin_0, RTC.5V, CR_Servo_(I).vcc, CR_Servo_(D).vcc, Parte1.5V
  N1: LCD.V0, R1.WIPER
  N2: LCD.RS, Parte1.D43
  GND: LCD.R/W, LCD.LED-, PIR.GND, LED_D.common_anode, LED_I.common_anode, STD_Servo_(I).gnd, STD_Servo_(D).gnd, R1.CCW, RTC.GND, CR_Servo_(I).gnd, Parte1.GND
  N3: LCD.E, Parte1.D41
  N4: LCD.DB4, Parte1.D33
  N5: LCD.DB5, Parte1.D35
  N6: LCD.DB6, Parte1.D37
  N7: LCD.DB7, Parte1.D39
  N8: LCD.LED+, R2.Pin_1
  N9: PIR.SIG, Parte1.D31
  N10: LED_D.red_cathode, R3.Pin_0
  N11: LED_D.green_cathode, R4.Pin_0
  N12: LED_D.blue_cathode, R5.Pin_0
  N13: LED_I.red_cathode, R6.Pin_0
  N14: LED_I.green_cathode, R7.Pin_0
  N15: LED_I.blue_cathode, R8.Pin_0
  N16: STD_Servo_(I).pulse, Parte1.D23
  N17: STD_Servo_(D).pulse, Parte1.D22
  N18: RTC.SCL, Parte1.D21/SCL
  N19: RTC.SDA, Parte1.D20/SDA
  N20: R3.Pin_1, R6.Pin_1, Parte1.D45
  N21: R4.Pin_1, R7.Pin_1, Parte1.D46, Parte1.D47
  N22: R5.Pin_1, R8.Pin_1
  N23: CR_Servo_(I).pulse, Parte1.D25
  N24: CR_Servo_(D).pulse, Parte1.D24
  N25: R10.Pin_0, Sensor_cap_2.T2, Parte1.D50
  N26: R10.Pin_1, R11.Pin_1, R12.Pin_1, Parte1.D48
  N27: Sensor_cap_1.T1, Sensor_cap_1.T2, R11.Pin_0, Parte1.D49
  N28: Sensor_cap_3.T2, R12.Pin_0, Parte1.D51
